# Fritzing sketch wiring (saved by Fritzing 1.0.6)

parts:
  A1 = Raspberry Pi Pico2
  RE1 = KY-040 Rotary encoder [package="Breakout board"]
  S1 = Pushbutton [package="[THT]"]
  Adafruit_DVI_Sock_for_Pico1 = Adafruit DVI Sock for Pico [part_number=#5957]

nets:
  N1: A1.pin_5, RE1.SW
  N2: A1.pin_6, RE1.DT
  N3: A1.pin_7, S1.Pin_3
  GND: A1.pin_8, A1.pin_18, A1.pin_23, A1.pin_33, A1.pin_38, RE1.GND, RE1.CLK, Adafruit_DVI_Sock_for_Pico1.GND
  N4: A1.pin_9, S1.Pin_1
  N5: A1.pin_16, Adafruit_DVI_Sock_for_Pico1.D0P
  N6: A1.pin_17, Adafruit_DVI_Sock_for_Pico1.D0N
  N7: A1.pin_19, Adafruit_DVI_Sock_for_Pico1.CKP
  N8: A1.pin_20, Adafruit_DVI_Sock_for_Pico1.CKN
  N9: A1.pin_21, Adafruit_DVI_Sock_for_Pico1.D2P
  N10: A1.pin_22, Adafruit_DVI_Sock_for_Pico1.D2N
  N11: A1.pin_24, Adafruit_DVI_Sock_for_Pico1.D1P
  N12: A1.pin_25, Adafruit_DVI_Sock_for_Pico1.D1N
  N13: A1.pin_36, RE1.Vcc

custom parts:
  Raspberry Pi Pico2: Raspberry Pi Pico 2W is our new $7 microcontroller board, built on RP2350: our new high-performance, secure microcontroller with on board WiFi.
  KY-040 Rotary encoder: KY-040 Rotary Encoder with switch on breakout borad from AZ Delivery
  Adafruit DVI Sock for Pico: Wouldn't it be cool to display images and graphics directly from your Pico or Pico W to an HDMI monitor or television? We think so! So we designed this DVI Sock with a digital video output (a.k.a DVI) that will work with any HDMI monitor or display. Note it doesn't do audio, just graphics! We designed this little breakout board after seeing Wren6991's Pico DVI Sock and their cool demos of the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
